# Fritzing sketch SchmittTrigger-AMP-opto-2018-08-19 (saved by Fritzing 0.9.3b)
breadboards: 1

parts:
  U1 = LM 358 Dual Op-Amp [package="DIP8 [THT]"]
  IC1 = IC, DIP package, 4 pins [chip_label=IC]
  IC2 = IC, DIP package, 4 pins [chip_label=IC]
  R1 = Resistor [tolerance=±5% resistance=33k package=THT]
  R2 = Resistor [tolerance=±5% resistance=47k package=THT]
  R3 = Resistor [tolerance=±5% resistance=220 package=THT]
  R4 = Resistor [tolerance=±5% resistance=33k package=THT]
  R5 = Resistor [tolerance=±5% resistance=10k package=THT]
  R6 = Resistor [tolerance=±5% resistance=47k package=THT]
  R7 = Resistor [tolerance=±5% resistance=220 package=THT]
  R8 = Resistor [tolerance=±5% resistance=220 package=THT]
  IC3 = IC, DIP package, 8 pins [chip_label=IC]
  IC4 = IC, DIP package, 8 pins [chip_label=IC]
  L1 = Inductor [package="400 mil [THT]"]
  L2 = Inductor [package="400 mil [THT]"]

nets:
  N1: U1.connector0, R2.Pin_0, R8.Pin_1
  N2: U1.connector1, IC3.pin6
  N3: U1.connector2, R1.Pin_1, R2.Pin_1, R3.Pin_1
  N4: U1.connector3, IC1.pin2, IC2.pin2, R3.Pin_0, R5.Pin_1, IC3.pin4, IC4.pin4
  N5: U1.connector4, R4.Pin_0, R5.Pin_0, R6.Pin_1
  N6: U1.connector5, IC4.pin6
  N7: U1.connector6, R6.Pin_0, R7.Pin_0
  N8: U1.connector7, R1.Pin_0, R4.Pin_1, IC3.pin1, IC4.pin1
  N9: IC1.pin1, R8.Pin_0
  N10: IC2.pin1, R7.Pin_1
  N11: IC3.pin2, L1.pin_1
  N12: IC3.pin3, L1.pin_0
  N13: IC4.pin2, L2.pin_1
  N14: IC4.pin3, L2.pin_0

notes:
  to 5volts power
