# Fritzing sketch spaghetti-ina169 (saved by Fritzing 0.9.3b)
breadboards: 1

parts:
  U1 = mystery part, 5 pins [chip_label=ina169]
  VCC1 = Battery

nets:
  N1: U1.pin4, VCC1.+
  N2: U1.pin5, VCC1.-

notes:
  gpio-gnd
  mcp3008-gnd
  (vout)mcp3008-a2
  12 volt feed
  (vin-)To + on motor HAT (motor power)
  (vcc)gpio 3.3 volt
  vcc - vout - vin- - vin+ - gnd
