# Fritzing sketch amp-coil-rpizero-transistor-20180815 (saved by Fritzing 0.9.3b)
breadboards: 1

parts:
  Q1 = NPN-Transistor [package="TO92 [THT]"]
  R1 = Resistor [tolerance=±5% resistance=470k package=THT]
  R2 = Resistor [tolerance=±5% resistance=1M package=THT]
  U1 = mystery part, 6 pins [chip_label=amp]
  VCC1 = Battery
  L1 = Inductor [package="400 mil [THT]"]
  MCU1 = Raspberry Pi Zero

nets:
  N1: Q1.E, MCU1.pin_18
  N2: Q1.B, R1.Pin_1, R2.Pin_0
  N3: Q1.C, R1.Pin_0, U1.pin1, VCC1.-
  N4: R2.Pin_1, U1.pin4
  N5: U1.pin3, L1.pin_0
  N6: U1.pin5, L1.pin_1
  N7: U1.pin6, VCC1.+

notes:
  5v power
  to GPIO24/25 on RPi
  pin order amp: gnd-gnd-gnd-out-in-vcc
  finally learnt that all gnd are the same
  470kOhm resistor
  1 Mohm resistor
