# Fritzing sketch spaghetti-bwf-opto (saved by Fritzing 0.9.3b)
breadboards: 1

parts:
  Q1 = NPN-Transistor [part_number=bc547b package="TO92 [THT]"]
  R1 = Resistor [tolerance=±5% resistance=2.2k package=THT]
  IC1 = IC, DIP package, 4 pins [chip_label=el816]  # not connected
  R2 = Resistor [tolerance=±5% resistance=220 package=THT]
  R3 = Resistor [tolerance=±5% resistance=220 package=THT]
  VCC1 = 4 x AAA Battery Mount
  U1 = mystery part, 5 pins [chip_label="lm386 board"]
  L1 = Inductor [package="400 mil [THT]"]

nets:
  N1: Q1.E, R2.Pin_1
  N2: Q1.B, R1.Pin_1
  N3: Q1.C, VCC1.+, U1.pin2
  N4: R1.Pin_0, U1.pin3
  N5: R2.Pin_0, R3.Pin_1
  N6: R3.Pin_0, VCC1.-, U1.pin1
  N7: U1.pin4, L1.pin_0
  N8: U1.pin5, L1.pin_1

notes:
  gpio-gnd
  gpio24 or 25
  gnd
  vcc
  out
  join all GND pins
  el816
